# Fritzing sketch temp (saved by Fritzing 0.9.3b)
breadboards: 1

parts:
  Part1 = Arduino Uno (Rev3) - ICSP
  R2 = Resistor [tolerance=±5% resistance=100k package="2512 [SMD]"]
  R1 = Temperature Sensor (Thermistor) [thermistor_type=NTC package=THT]

nets:
  N1: Part1.A0, R2.Pin_1, R1.pin_1
  N2: Part1.5V, R1.pin_0
  N3: Part1.GND, R2.Pin_0
